# Fritzing sketch Arduino LED Battery Monitor (saved by Fritzing 0.7.12b)
breadboards: 1

parts:
  Arduino1 = Arduino
  VCC1 = Battery block 9V
  R1 = Resistor [tolerance=±5% resistance=1k package=THT]
  R2 = Resistor [tolerance=±5% resistance=1k package=THT]
  R3 = Resistor [tolerance=±5% resistance=220 package=THT]
  LED1 = LED - 5mm [color="Red (633nm)" package="5 mm [THT]"]
  LED2 = LED - 5mm [color="Red (633nm)" package="5 mm [THT]"]
  LED3 = LED - 5mm [color="Red (633nm)" package="5 mm [THT]"]
  LED4 = LED - 5mm [color="Red (633nm)" package="5 mm [THT]"]
  LED5 = LED - 5mm [color="Red (633nm)" package="5 mm [THT]"]
  LED6 = LED - 5mm [color="Red (633nm)" package="5 mm [THT]"]
  LED7 = LED - 5mm [color="Red (633nm)" package="5 mm [THT]"]
  LED8 = LED - 5mm [color="Red (633nm)" package="5 mm [THT]"]
  LED9 = LED - 5mm [color="Red (633nm)" package="5 mm [THT]"]
  LED10 = LED - 5mm [color="Red (633nm)" package="5 mm [THT]"]
  R4 = Resistor [tolerance=±5% resistance=330 package=THT]
  R5 = Resistor [tolerance=±5% resistance=330 package=THT]
  R6 = Resistor [tolerance=±5% resistance=330 package=THT]
  R7 = Resistor [tolerance=±5% resistance=330 package=THT]
  R8 = Resistor [tolerance=±5% resistance=330 package=THT]
  R9 = Resistor [tolerance=±5% resistance=330 package=THT]
  R10 = Resistor [tolerance=±5% resistance=330 package=THT]
  R11 = Resistor [tolerance=±5% resistance=330 package=THT]
  R12 = Resistor [tolerance=±5% resistance=330 package=THT]
  R13 = Resistor [tolerance=±5% resistance=330 package=THT]

nets:
  N1: Arduino1.GND, LED1.anode, LED2.anode, LED3.anode, LED4.anode, LED5.anode, LED6.anode, LED7.anode, LED8.anode, LED9.anode, LED10.anode
  N2: Arduino1.D9, R4.Pin_0
  N3: Arduino1.D8, R5.Pin_0
  N4: Arduino1.D7, R6.Pin_0
  N5: Arduino1.D6, R7.Pin_0
  N6: Arduino1.D5, R8.Pin_0
  N7: Arduino1.D4, R9.Pin_0
  N8: Arduino1.D3, R10.Pin_0
  N9: Arduino1.D2, R11.Pin_0
  N10: Arduino1.D1TX, R12.Pin_0
  N11: Arduino1.D0RX, R13.Pin_0
  N12: Arduino1.A0, R1.Pin_1, R3.Pin_1
  N13: VCC1.-, R2.Pin_0
  N14: VCC1.+, R1.Pin_0
  N15: R2.Pin_1, R3.Pin_0
  N16: LED1.cathode, R4.Pin_1
  N17: LED2.cathode, R5.Pin_1
  N18: LED3.cathode, R6.Pin_1
  N19: LED4.cathode, R7.Pin_1
  N20: LED5.cathode, R8.Pin_1
  N21: LED6.cathode, R9.Pin_1
  N22: LED7.cathode, R10.Pin_1
  N23: LED8.cathode, R11.Pin_1
  N24: LED9.cathode, R12.Pin_1
  N25: LED10.cathode, R13.Pin_1
